# Fritzing sketch esp_flight_controller_v0_1 (saved by Fritzing 0.9.4)
perfboards: 1

parts:
  J1 = male pin header, 3 pins [form="♂ (male)"]
  J2 = male pin header, 3 pins [form="♂ (male)"]
  J3 = male pin header, 3 pins [form="♂ (male)"]
  J4 = male pin header, 3 pins [form="♂ (male)"]
  U1 = ESP32-38PinWide [part_number=ESP32-38PinWide]
  MPU9250_MPU-1 = SparkFun IMU Breakout - MPU-9250 [part_number=" SEN-13762"]

nets:
  N1: J1.pin1, U1.GPIO27
  N2: J1.pin2, J2.pin2, J3.pin2, J4.pin2, U1.VIN
  N3: J1.pin3, J2.pin3, J3.pin3, J4.pin3, U1.GPIO11
  N4: J2.pin1, U1.GPIO14
  N5: J3.pin1, U1.GPIO12
  N6: J4.pin1, U1.GPIO13
  N7: U1.3.3, MPU9250_MPU-1.VDD
  N8: U1.GPIO34, MPU9250_MPU-1.INT
  GND: U1.GND, MPU9250_MPU-1.GND
  N9: U1.GPIO5, MPU9250_MPU-1.!CS
  N10: U1.GPIO18, MPU9250_MPU-1.SCL/SCLK
  N11: U1.GPIO19, MPU9250_MPU-1.AD0/SDO
  N12: U1.GPIO23, MPU9250_MPU-1.SDA/SDI

notes:
  ESC Pins

custom parts:
  ESP32-38PinWide: Generic 38-Pin ESP32 with wide format (only access to one side of pins on a breadboard) based on Stephen Lilley's HiLetgo ESP-WROOM-32 ESP32 ESP-32S Development Board.
  SparkFun IMU Breakout - MPU-9250: The SparkFun MPU-9250 IMU Breakout features the latest 9-axis MEMS sensor from InvenSense. Each of these 9DoF breakouts feature an MPU-9250 with a System in Package (SiP) that combines two chips: the MPU-6500, which contains a 3-axis gyroscope as well as a 3-axis accelerometer, and the AK8963, which features a 3-axis magnetometer. This breakout has been designed to be smaller than some of our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
